# Fritzing sketch LM35 (saved by Fritzing 0.9.3b)
breadboards: 1

parts:
  T1 = LM35 Temperature Sensor [package="TO92 [THT]"]
  Componente1 = Arduino Uno (Rev3)

nets:
  N1: T1.+Vs, Componente1.5V
  GND: T1.GND, Componente1.GND
